// Logisim project CORGProjectPart1.circ as structural Verilog
module twosComplement (
  input  [7:0] X,
  output [7:0] COMPL
);

  wire [7:0] not_1_out;

  assign not_1_out = ~X;  // NOT_Gate not_1, 8 bits wide
  FULLADDER8 fulladder8_1 (.X(not_1_out), .Y(8'h1), .CIN(1'b0), .SUM(COMPL));  // open: COUT
endmodule

module rotl (
  input  [7:0] X,
  input  [2:0] Y,
  output [7:0] Z
);

  Multiplexer #(.select(3)) multiplexer_1 (
    .in0(X[7]), .in1(X[6]), .in2(X[5]), .in3(X[4]), .in4(X[3]), .in5(X[2]), .in6(X[1]), .in7(X[0]),
    .out(Z[7]), .sel(Y));
  Multiplexer #(.select(3)) multiplexer_2 (
    .in0(X[6]), .in1(X[5]), .in2(X[4]), .in3(X[3]), .in4(X[2]), .in5(X[1]), .in6(X[0]), .in7(X[7]),
    .out(Z[6]), .sel(Y));
  Multiplexer #(.select(3)) multiplexer_3 (
    .in0(X[5]), .in1(X[4]), .in2(X[3]), .in3(X[2]), .in4(X[1]), .in5(X[0]), .in6(X[7]), .in7(X[6]),
    .out(Z[5]), .sel(Y));
  Multiplexer #(.select(3)) multiplexer_4 (
    .in0(X[4]), .in1(X[3]), .in2(X[2]), .in3(X[1]), .in4(X[0]), .in5(X[7]), .in6(X[6]), .in7(X[5]),
    .out(Z[4]), .sel(Y));
  Multiplexer #(.select(3)) multiplexer_5 (
    .in0(X[3]), .in1(X[2]), .in2(X[1]), .in3(X[0]), .in4(X[7]), .in5(X[6]), .in6(X[5]), .in7(X[4]),
    .out(Z[3]), .sel(Y));
  Multiplexer #(.select(3)) multiplexer_6 (
    .in0(X[2]), .in1(X[1]), .in2(X[0]), .in3(X[7]), .in4(X[6]), .in5(X[5]), .in6(X[4]), .in7(X[3]),
    .out(Z[2]), .sel(Y));
  Multiplexer #(.select(3)) multiplexer_7 (
    .in0(X[1]), .in1(X[0]), .in2(X[7]), .in3(X[6]), .in4(X[5]), .in5(X[4]), .in6(X[3]), .in7(X[2]),
    .out(Z[1]), .sel(Y));
  Multiplexer #(.select(3)) multiplexer_8 (
    .in0(X[0]), .in1(X[7]), .in2(X[6]), .in3(X[5]), .in4(X[4]), .in5(X[3]), .in6(X[2]), .in7(X[1]),
    .out(Z[0]), .sel(Y));
endmodule

module rotr (
  input  [7:0] X,
  input  [2:0] Y,
  output [7:0] Z
);

  Multiplexer #(.select(3)) multiplexer_1 (
    .in0(X[0]), .in1(X[1]), .in2(X[2]), .in3(X[3]), .in4(X[4]), .in5(X[5]), .in6(X[6]), .in7(X[7]),
    .out(Z[0]), .sel(Y));
  Multiplexer #(.select(3)) multiplexer_2 (
    .in0(X[1]), .in1(X[2]), .in2(X[3]), .in3(X[4]), .in4(X[5]), .in5(X[6]), .in6(X[7]), .in7(X[0]),
    .out(Z[1]), .sel(Y));
  Multiplexer #(.select(3)) multiplexer_3 (
    .in0(X[2]), .in1(X[3]), .in2(X[4]), .in3(X[5]), .in4(X[6]), .in5(X[7]), .in6(X[0]), .in7(X[1]),
    .out(Z[2]), .sel(Y));
  Multiplexer #(.select(3)) multiplexer_4 (
    .in0(X[3]), .in1(X[4]), .in2(X[5]), .in3(X[6]), .in4(X[7]), .in5(X[0]), .in6(X[1]), .in7(X[2]),
    .out(Z[3]), .sel(Y));
  Multiplexer #(.select(3)) multiplexer_5 (
    .in0(X[4]), .in1(X[5]), .in2(X[6]), .in3(X[7]), .in4(X[0]), .in5(X[1]), .in6(X[2]), .in7(X[3]),
    .out(Z[4]), .sel(Y));
  Multiplexer #(.select(3)) multiplexer_6 (
    .in0(X[5]), .in1(X[6]), .in2(X[7]), .in3(X[0]), .in4(X[1]), .in5(X[2]), .in6(X[3]), .in7(X[4]),
    .out(Z[5]), .sel(Y));
  Multiplexer #(.select(3)) multiplexer_7 (
    .in0(X[6]), .in1(X[7]), .in2(X[0]), .in3(X[1]), .in4(X[2]), .in5(X[3]), .in6(X[4]), .in7(X[5]),
    .out(Z[6]), .sel(Y));
  Multiplexer #(.select(3)) multiplexer_8 (
    .in0(X[7]), .in1(X[0]), .in2(X[1]), .in3(X[2]), .in4(X[3]), .in5(X[4]), .in6(X[5]), .in7(X[6]),
    .out(Z[7]), .sel(Y));
endmodule

module FULLADDER8 (
  input  [7:0] X,
  input  [7:0] Y,
  input  CIN,
  output [7:0] SUM,
  output COUT
);

  wire and_1_out, and_2_out, and_3_out, and_4_out, and_5_out, and_6_out, and_7_out, and_8_out, and_9_out,
       and_10_out, and_11_out, and_12_out, and_13_out, and_14_out, and_15_out, and_16_out, or_1_out,
       or_2_out, or_3_out, or_4_out, or_5_out, or_6_out, or_7_out, xor_1_out, xor_2_out, xor_3_out,
       xor_4_out, xor_5_out, xor_6_out, xor_7_out, xor_8_out;

  xor xor_1 (xor_1_out, X[0], Y[0]);
  and and_1 (and_1_out, Y[0], X[0]);
  xor xor_2 (xor_2_out, X[1], Y[1]);
  and and_2 (and_2_out, Y[1], X[1]);
  xor xor_3 (xor_3_out, X[2], Y[2]);
  and and_3 (and_3_out, Y[2], X[2]);
  xor xor_4 (xor_4_out, X[3], Y[3]);
  and and_4 (and_4_out, Y[3], X[3]);
  xor xor_5 (xor_5_out, X[4], Y[4]);
  and and_5 (and_5_out, Y[4], X[4]);
  xor xor_6 (xor_6_out, X[5], Y[5]);
  and and_6 (and_6_out, Y[5], X[5]);
  xor xor_7 (xor_7_out, X[6], Y[6]);
  and and_7 (and_7_out, Y[6], X[6]);
  xor xor_8 (xor_8_out, X[7], Y[7]);
  and and_8 (and_8_out, Y[7], X[7]);
  and and_9 (and_9_out, xor_1_out, CIN);
  and and_10 (and_10_out, xor_2_out, or_1_out);
  and and_11 (and_11_out, xor_3_out, or_2_out);
  and and_12 (and_12_out, xor_4_out, or_3_out);
  and and_13 (and_13_out, xor_5_out, or_4_out);
  and and_14 (and_14_out, xor_6_out, or_5_out);
  and and_15 (and_15_out, xor_7_out, or_6_out);
  and and_16 (and_16_out, xor_8_out, or_7_out);
  xor xor_9 (SUM[0], xor_1_out, CIN);
  or or_1 (or_1_out, and_9_out, and_1_out);
  xor xor_10 (SUM[1], xor_2_out, or_1_out);
  or or_2 (or_2_out, and_10_out, and_2_out);
  xor xor_11 (SUM[2], xor_3_out, or_2_out);
  or or_3 (or_3_out, and_11_out, and_3_out);
  xor xor_12 (SUM[3], xor_4_out, or_3_out);
  or or_4 (or_4_out, and_12_out, and_4_out);
  xor xor_13 (SUM[4], xor_5_out, or_4_out);
  or or_5 (or_5_out, and_13_out, and_5_out);
  xor xor_14 (SUM[5], xor_6_out, or_5_out);
  or or_6 (or_6_out, and_14_out, and_6_out);
  xor xor_15 (SUM[6], xor_7_out, or_6_out);
  or or_7 (or_7_out, and_15_out, and_7_out);
  xor xor_16 (SUM[7], xor_8_out, or_7_out);
  or or_8 (COUT, and_16_out, and_8_out);
endmodule

module fullAdder (
  input  I1,
  input  I2,
  input  Cin1,
  output Sum,
  output Cout
);

  wire and_1_out, and_2_out, xor_1_out;

  xor xor_1 (xor_1_out, I1, I2);
  and and_1 (and_1_out, I1, I2);
  and and_2 (and_2_out, xor_1_out, Cin1);
  xor xor_2 (Sum, xor_1_out, Cin1);
  or or_1 (Cout, and_2_out, and_1_out);
endmodule

module twoBitFullAdder (
  input  X0,
  input  X1,
  input  Y0,
  input  Y1,
  input  Cin,
  output S0,
  output S1,
  output Cout
);

  wire fulladder_1_cout;

  fullAdder fulladder_1 (.I1(X0), .I2(X1), .Cin1(Cin), .Sum(S0), .Cout(fulladder_1_cout));
  fullAdder fulladder_2 (.I1(Y0), .I2(Y1), .Cin1(fulladder_1_cout), .Sum(S1), .Cout(Cout));
endmodule

module fourBitFullAdder (
  input  X0,
  input  Y0,
  input  X1,
  input  Y1,
  input  X2,
  input  Y2,
  input  X3,
  input  Y3,
  input  Cin,
  output S0,
  output S1,
  output S2,
  output S3,
  output Cout
);

  wire twobitfulladder_1_cout;

  twoBitFullAdder twobitfulladder_1 (
    .X0(X0), .X1(Y0), .Y0(X1), .Y1(Y1), .Cin(Cin), .S0(S0), .S1(S1), .Cout(twobitfulladder_1_cout));
  twoBitFullAdder twobitfulladder_2 (
    .X0(X2), .X1(Y2), .Y0(X3), .Y1(Y3), .Cin(twobitfulladder_1_cout), .S0(S2), .S1(S3), .Cout(Cout));
endmodule

module eightBitFullAdder (
  input  [7:0] X,
  input  [7:0] Y,
  input  Cin,
  output [7:0] Sum,
  output Cout
);

  wire fourbitfulladder_1_cout;

  fourBitFullAdder fourbitfulladder_1 (
    .X0(X[0]), .Y0(Y[0]), .X1(X[1]), .Y1(Y[1]), .X2(X[2]), .Y2(Y[2]), .X3(X[3]), .Y3(Y[3]), .Cin(Cin),
    .S0(Sum[0]), .S1(Sum[1]), .S2(Sum[2]), .S3(Sum[3]), .Cout(fourbitfulladder_1_cout));
  fourBitFullAdder fourbitfulladder_2 (
    .X0(X[4]), .Y0(Y[4]), .X1(X[5]), .Y1(Y[5]), .X2(X[6]), .Y2(Y[6]), .X3(X[7]), .Y3(Y[7]), .S0(Sum[4]),
    .S1(Sum[5]), .S2(Sum[6]), .S3(Sum[7]), .Cout(Cout));  // open: Cin
endmodule

module customComparator (
  input  [7:0] X,
  input  [7:0] Y,
  output EQUAL
);

  wire xnor_1_out, xnor_2_out, xnor_3_out, xnor_4_out, xnor_5_out, xnor_6_out, xnor_7_out, xnor_8_out;

  xnor xnor_1 (xnor_1_out, X[0], Y[0]);
  xnor xnor_2 (xnor_2_out, X[1], Y[1]);
  xnor xnor_3 (xnor_3_out, X[2], Y[2]);
  xnor xnor_4 (xnor_4_out, X[3], Y[3]);
  xnor xnor_5 (xnor_5_out, X[4], Y[4]);
  xnor xnor_6 (xnor_6_out, X[5], Y[5]);
  xnor xnor_7 (xnor_7_out, X[6], Y[6]);
  xnor xnor_8 (xnor_8_out, X[7], Y[7]);
  and and_1 (EQUAL, xnor_1_out, xnor_2_out, xnor_3_out, xnor_4_out, xnor_5_out, xnor_6_out, xnor_7_out, xnor_8_out);
endmodule

module ALU8 (
  input  [7:0] X,
  input  [1:0] OP,
  input  [7:0] Y,
  output CF,
  output ZF,
  output SF,
  output [7:0] RESULT,
  output EQ,
  output OVF
);

  wire and_2_out, and_3_out, and_4_out, and_5_out, not_1_out, not_2_out, not_3_out, or_3_out;
  wire [7:0] and_1_out, fulladder8_1_sum, multiplexer_1_out, multiplexer_2_out, or_1_out, rotr_1_z,
       twoscomplement_1_compl, twoscomplement_2_compl;

  assign or_1_out = X | Y;  // OR_Gate or_1, 8 bits wide
  assign and_1_out = X & Y;  // AND_Gate and_1, 8 bits wide
  and and_2 (and_2_out, X[7], Y[7]);
  not not_1 (not_1_out, X[7]);
  not not_2 (not_2_out, Y[7]);
  FULLADDER8 fulladder8_1 (.X(multiplexer_1_out), .Y(multiplexer_2_out), .CIN(1'b0), .SUM(fulladder8_1_sum), .COUT(CF));
  rotr rotr_1 (.X(X), .Y(3'b001), .Z(rotr_1_z));
  customComparator customcomparator_1 (.X(X), .Y(Y), .EQUAL(EQ));
  and and_3 (and_3_out, not_1_out, not_2_out);
  not not_3 (not_3_out, fulladder8_1_sum[7]);
  Multiplexer #(.width(8)) multiplexer_1 (.in0(Y), .in1(twoscomplement_1_compl), .out(multiplexer_1_out), .sel(Y[7]));
  twosComplement twoscomplement_1 (.X(Y), .COMPL(twoscomplement_1_compl));
  Multiplexer #(.width(8)) multiplexer_2 (.in0(X), .in1(twoscomplement_2_compl), .out(multiplexer_2_out), .sel(X[7]));
  twosComplement twoscomplement_2 (.X(X), .COMPL(twoscomplement_2_compl));
  and and_4 (and_4_out, and_2_out, not_3_out);
  Multiplexer #(.select(2), .width(8)) multiplexer_3 (
    .in0(fulladder8_1_sum), .in1(or_1_out), .in2(and_1_out), .in3(rotr_1_z), .out(RESULT), .sel(OP));
  and and_5 (and_5_out, and_3_out, fulladder8_1_sum[7]);
  or or_2 (OVF, and_4_out, and_5_out);
  or or_3 (or_3_out, fulladder8_1_sum[0], fulladder8_1_sum[1], fulladder8_1_sum[2], fulladder8_1_sum[3], fulladder8_1_sum[4], fulladder8_1_sum[5], fulladder8_1_sum[6], fulladder8_1_sum[7]);
  not not_4 (ZF, or_3_out);

  assign SF = RESULT[7];
endmodule
